// Logisim project cpu.circ as structural Verilog: 10 circuits, main circuit main
module main (
  input  in_1,
  output [31:0] out_2
);

  wire alu_lb_t, alu_src_t, alu_zero_t, and_3_out, and_4_out, and_6_out, and_7_out, clk_t, ctrl_valid,
       display_w_t, mem_w_t, or_1_out, pc_src_t, read_valid_t, reg_w_t, screen_w_t, we_t;
  wire [1:0] scnd_add_src_t, wb_src_t;
  wire [2:0] f3_t, imm_src_t;
  wire [3:0] alu_ctrl_t, mask_t, register_1_q, register_1_q_2;
  wire [13:0] multiplexer_1_out, outPC_plus_4_t, outPC_t;
  wire [31:0] alu_addr_t, and_2_out, bit_extender_1_out, bit_extender_2_out, branch_val_t, data_b_t,
       instructionmemory_1_data, mem_data_t, multiplexer_3_out, registerfile_1_rs2, rs1_t, shifter_1_out,
       signextender_1_data_out, wb_data_t, wd_t;
  wire [31:8] register_1_q_3;

  Clock clock_1 (.out(clk_t));
  Multiplexer #(.width(14)) multiplexer_1 (
    .in0(outPC_plus_4_t), .in1(branch_val_t[13:0]), .out(multiplexer_1_out), .sel(pc_src_t));
  Adder #(.width(14)) adder_1 (.a(outPC_t), .b(14'h4), .out(outPC_plus_4_t));  // open: cin, cout
  ProgramCounter programcounter_1 (.inPC(multiplexer_1_out), .clk(clk_t), .reset(in_1), .outPC(outPC_t));
  or or_1 (or_1_out, ctrl_valid, read_valid_t);
  and and_1 (we_t, reg_w_t, or_1_out);
  InstructionMemory instructionmemory_1 (
    .addr(outPC_t), .data({instructionmemory_1_data[31:15], f3_t, instructionmemory_1_data[11:0]}));
  ControlLogic controllogic_1 (
    .op(instructionmemory_1_data[6:0]), .func3(f3_t), .func7(instructionmemory_1_data[31:25]),
    .alu_zero(alu_zero_t), .alu_lb(alu_lb_t), .alu_control(alu_ctrl_t), .alu_src(alu_src_t),
    .imm_src(imm_src_t), .wb_src(wb_src_t), .mem_write(mem_w_t), .pc_src(pc_src_t), .reg_write(reg_w_t),
    .second_add_src(scnd_add_src_t), .data_valid(ctrl_valid));
  RegisterFile registerfile_1 (
    .rsi1(instructionmemory_1_data[19:15]), .rsi2(instructionmemory_1_data[24:20]),
    .rdi(instructionmemory_1_data[11:7]), .reset(in_1), .rd(out_2), .we(we_t), .clk(clk_t), .rs1(rs1_t),
    .rs2(registerfile_1_rs2));
  SignExtender signextender_1 (
    .raw_data({instructionmemory_1_data[31:15], f3_t, instructionmemory_1_data[11:7]}), .imm_src(imm_src_t),
    .data_out(signextender_1_data_out));
  Multiplexer #(.width(32)) multiplexer_2 (
    .in0(registerfile_1_rs2), .in1(signextender_1_data_out), .out(data_b_t), .sel(alu_src_t));
  TTY tty_1 (.data(wd_t[6:0]), .clk(clk_t), .we(screen_w_t), .clr(in_1));
  assign bit_extender_1_out = {{18{1'b0}}, outPC_t};  // Bit_Extender bit_extender_1
  ALU alu_1 (
    .dataA(rs1_t), .dataB(data_b_t), .sel(alu_ctrl_t), .dataD(alu_addr_t), .zero(alu_zero_t),
    .last_bit(alu_lb_t));
  Multiplexer #(.select(2), .width(32)) multiplexer_3 (
    .in0(bit_extender_1_out), .in1({32{1'b0}}), .in2(rs1_t), .out(multiplexer_3_out), .sel(scnd_add_src_t));  // open: in3
  Shifter #(.shift("lr"), .width(32)) shifter_1 (.in(wd_t), .\dist (5'b01000), .out(shifter_1_out));
  Hex_Digit_Display hex_digit_display_1 (.value(register_1_q_2));  // open: dp
  Register #(.width(32)) register_1 (
    .D(shifter_1_out), .en(display_w_t), .clk(clk_t), .Q({register_1_q_3, register_1_q_2, register_1_q}),
    .clr(in_1));
  Adder #(.width(32)) adder_2 (
    .a(multiplexer_3_out), .b(signextender_1_data_out), .out(branch_val_t));  // open: cin, cout
  Hex_Digit_Display hex_digit_display_2 (.value(register_1_q));  // open: dp
  assign and_2_out = alu_addr_t & 32'hfffffffc;  // AND_Gate and_2, 32 bits wide
  LoadStoreDecoder loadstoredecoder_1 (
    .alu_addr(alu_addr_t), .f3(f3_t), .reg_read(registerfile_1_rs2), .byte_enable(mask_t), .data(wd_t));
  and and_3 (and_3_out, ~alu_addr_t[0], 1'b1);  // AND_Gate
  and and_4 (and_4_out, 1'b1, alu_addr_t[31]);
  and and_5 (screen_w_t, and_3_out, mem_w_t, and_4_out);
  DataMemory datamemory_1 (
    .addr(and_2_out), .wd(wd_t), .clk(clk_t), .we(mem_w_t), .mask(mask_t), .data_out(mem_data_t));
  assign bit_extender_2_out = {{18{1'b0}}, outPC_plus_4_t};  // Bit_Extender bit_extender_2
  Reader reader_1 (.mem_data(mem_data_t), .mask(mask_t), .f3(f3_t), .wb_data(wb_data_t), .valid(read_valid_t));
  and and_6 (and_6_out, alu_addr_t[0], 1'b1);
  and and_7 (and_7_out, 1'b1, alu_addr_t[31]);
  and and_8 (display_w_t, and_6_out, mem_w_t, and_7_out);
  Multiplexer #(.select(2), .width(32)) multiplexer_4 (
    .in0(alu_addr_t), .in1(wb_data_t), .in2(bit_extender_2_out), .in3(branch_val_t), .out(out_2),
    .sel(wb_src_t));

  // Other names for the same wires on the sheet: out_data_t[31:0] = out_2; reset_t = in_1

  // Notes on the sheet:
  //   Data Validity
  //   I/O Devices
  //   Screen
  //   Digit Display
endmodule

module ALU (
  input  [31:0] dataA,
  input  [31:0] dataB,
  input  [3:0] sel,
  output [31:0] dataD,
  output zero,
  output last_bit
);

  wire comparator_1_lt, comparator_2_lt;
  wire [31:0] addOut_t, andOut_t, orOut_t, sllOut_t, sltOut_t, sltuOut_t, sraOut_t, srlOut_t, subOut_t,
       xorOut_t;

  Adder #(.width(32)) adder_1 (.a(dataA), .b(dataB), .out(addOut_t));  // open: cin, cout
  Subtractor #(.width(32)) subtractor_1 (.a(dataA), .b(dataB), .out(subOut_t));  // open: bin, bout
  Shifter #(.width(32)) shifter_1 (.in(dataA), .\dist (dataB[4:0]), .out(sllOut_t));
  Comparator #(.width(32)) comparator_1 (.a(dataA), .b(dataB), .lt(comparator_1_lt));  // open: gt, eq
  Comparator #(.mode("unsigned"), .width(32)) comparator_2 (
    .a(dataA), .b(dataB), .lt(comparator_2_lt));  // open: gt, eq
  assign xorOut_t = dataA ^ dataB;  // XOR_Gate xor_1, 32 bits wide
  Shifter #(.shift("lr"), .width(32)) shifter_2 (.in(dataA), .\dist (dataB[4:0]), .out(srlOut_t));
  Shifter #(.shift("ar"), .width(32)) shifter_3 (.in(dataA), .\dist (dataB[4:0]), .out(sraOut_t));
  assign orOut_t = dataA | dataB;  // OR_Gate or_1, 32 bits wide
  assign andOut_t = dataA & dataB;  // AND_Gate and_1, 32 bits wide
  assign sltOut_t = {{31{1'b0}}, comparator_1_lt};  // Bit_Extender bit_extender_1
  assign sltuOut_t = {{31{1'b0}}, comparator_2_lt};  // Bit_Extender bit_extender_2
  Multiplexer #(.select(4), .width(32)) multiplexer_1 (
    .in0(addOut_t), .in1(subOut_t), .in2(andOut_t), .in3(orOut_t), .in4(sllOut_t), .in5(sltOut_t),
    .in6(srlOut_t), .in7(sltuOut_t), .in8(xorOut_t), .in9(sraOut_t), .out(dataD), .sel(sel));  // open: in10, in11, in12, in13, in14, in15
  Comparator #(.width(32)) comparator_3 (.a(dataD), .b({32{1'b0}}), .eq(zero));  // open: gt, lt

  assign last_bit = dataD[0];

  // Other names for the same wires on the sheet: dataA_t[31:0] = dataA; dataB_t[31:0] = dataB;
  //   dataBL5_t[4:0] = dataB[4:0]; dataD_t[31:0] = dataD; sel_t[3:0] = sel

  // Notes on the sheet:
  //   ALU
  //   Sel
  //   RV32I ALU Operations
  //   Operation
  //   0000      add - Sumation
  //   0001      sub - Subtraction
  //   0010      and - logical AND
  //   0011      or - logical OR
  //   0100      sll - Shift Left Logical
  //   0101      slt - Set Less Than
  //   0110      srl - Shift Right Logical
  //   0111      sltu - Set Less Than Unsigned
  //   1000      xor - eXclusive OR
  //   1001      sra - Shift Right Arithmetic
endmodule

module RegisterFile (
  input  [4:0] rsi1,
  input  [4:0] rsi2,
  input  [4:0] rdi,
  input  reset,
  input  [31:0] rd,
  input  we,
  input  clk,
  output [31:0] rs1,
  output [31:0] rs2
);

  wire x0we_t, x1we_t, x2we_t, x3we_t, x4we_t, x5we_t, x6we_t, x7we_t, x8we_t, x9we_t, x10we_t, x11we_t,
       x12we_t, x13we_t, x14we_t, x15we_t, x16we_t, x17we_t, x18we_t, x19we_t, x20we_t, x21we_t, x22we_t,
       x23we_t, x24we_t, x25we_t, x26we_t, x27we_t, x28we_t, x29we_t, x30we_t, x31we_t;
  wire [31:0] x1q_t, x2q_t, x3q_t, x4q_t, x5q_t, x6q_t, x7q_t, x8q_t, x9q_t, x10q_t, x11q_t, x12q_t, x13q_t,
       x14q_t, x15q_t, x16q_t, x17q_t, x18q_t, x19q_t, x20q_t, x21q_t, x22q_t, x23q_t, x24q_t, x25q_t,
       x26q_t, x27q_t, x28q_t, x29q_t, x30q_t, x31q_t;

  Demultiplexer #(.select(5)) demultiplexer_1 (
    .out0(x0we_t), .out1(x1we_t), .out2(x2we_t), .out3(x3we_t), .out4(x4we_t), .out5(x5we_t), .out6(x6we_t),
    .out7(x7we_t), .out8(x8we_t), .out9(x9we_t), .out10(x10we_t), .out11(x11we_t), .out12(x12we_t),
    .out13(x13we_t), .out14(x14we_t), .out15(x15we_t), .out16(x16we_t), .out17(x17we_t), .out18(x18we_t),
    .out19(x19we_t), .out20(x20we_t), .out21(x21we_t), .out22(x22we_t), .out23(x23we_t), .out24(x24we_t),
    .out25(x25we_t), .out26(x26we_t), .out27(x27we_t), .out28(x28we_t), .out29(x29we_t), .out30(x30we_t),
    .out31(x31we_t), .in(we), .sel(rdi));
  Register #(.width(32)) x4 (.D(rd), .en(x4we_t), .clk(clk), .Q(x4q_t), .clr(reset));
  Register #(.width(32)) x8 (.D(rd), .en(x8we_t), .clk(clk), .Q(x8q_t), .clr(reset));
  Register #(.width(32)) x12 (.D(rd), .en(x12we_t), .clk(clk), .Q(x12q_t), .clr(reset));
  Register #(.width(32)) x16 (.D(rd), .en(x16we_t), .clk(clk), .Q(x16q_t), .clr(reset));
  Register #(.width(32)) x20 (.D(rd), .en(x20we_t), .clk(clk), .Q(x20q_t), .clr(reset));
  Register #(.width(32)) x24 (.D(rd), .en(x24we_t), .clk(clk), .Q(x24q_t), .clr(reset));
  Register #(.width(32)) x28 (.D(rd), .en(x28we_t), .clk(clk), .Q(x28q_t), .clr(reset));
  Register #(.width(32)) x1 (.D(rd), .en(x1we_t), .clk(clk), .Q(x1q_t), .clr(reset));
  Register #(.width(32)) x5 (.D(rd), .en(x5we_t), .clk(clk), .Q(x5q_t), .clr(reset));
  Register #(.width(32)) x9 (.D(rd), .en(x9we_t), .clk(clk), .Q(x9q_t), .clr(reset));
  Register #(.width(32)) x13 (.D(rd), .en(x13we_t), .clk(clk), .Q(x13q_t), .clr(reset));
  Register #(.width(32)) x17 (.D(rd), .en(x17we_t), .clk(clk), .Q(x17q_t), .clr(reset));
  Register #(.width(32)) x21 (.D(rd), .en(x21we_t), .clk(clk), .Q(x21q_t), .clr(reset));
  Register #(.width(32)) x25 (.D(rd), .en(x25we_t), .clk(clk), .Q(x25q_t), .clr(reset));
  Register #(.width(32)) x29 (.D(rd), .en(x29we_t), .clk(clk), .Q(x29q_t), .clr(reset));
  Register #(.width(32)) x2 (.D(rd), .en(x2we_t), .clk(clk), .Q(x2q_t), .clr(reset));
  Register #(.width(32)) x6 (.D(rd), .en(x6we_t), .clk(clk), .Q(x6q_t), .clr(reset));
  Register #(.width(32)) x10 (.D(rd), .en(x10we_t), .clk(clk), .Q(x10q_t), .clr(reset));
  Register #(.width(32)) x14 (.D(rd), .en(x14we_t), .clk(clk), .Q(x14q_t), .clr(reset));
  Register #(.width(32)) x18 (.D(rd), .en(x18we_t), .clk(clk), .Q(x18q_t), .clr(reset));
  Register #(.width(32)) x22 (.D(rd), .en(x22we_t), .clk(clk), .Q(x22q_t), .clr(reset));
  Register #(.width(32)) x26 (.D(rd), .en(x26we_t), .clk(clk), .Q(x26q_t), .clr(reset));
  Register #(.width(32)) x30 (.D(rd), .en(x30we_t), .clk(clk), .Q(x30q_t), .clr(reset));
  Register #(.width(32)) x3 (.D(rd), .en(x3we_t), .clk(clk), .Q(x3q_t), .clr(reset));
  Register #(.width(32)) x7 (.D(rd), .en(x7we_t), .clk(clk), .Q(x7q_t), .clr(reset));
  Register #(.width(32)) x11 (.D(rd), .en(x11we_t), .clk(clk), .Q(x11q_t), .clr(reset));
  Register #(.width(32)) x15 (.D(rd), .en(x15we_t), .clk(clk), .Q(x15q_t), .clr(reset));
  Register #(.width(32)) x19 (.D(rd), .en(x19we_t), .clk(clk), .Q(x19q_t), .clr(reset));
  Register #(.width(32)) x23 (.D(rd), .en(x23we_t), .clk(clk), .Q(x23q_t), .clr(reset));
  Register #(.width(32)) x27 (.D(rd), .en(x27we_t), .clk(clk), .Q(x27q_t), .clr(reset));
  Register #(.width(32)) x31 (.D(rd), .en(x31we_t), .clk(clk), .Q(x31q_t), .clr(reset));
  Multiplexer #(.select(5), .width(32)) multiplexer_1 (
    .in0({32{1'b0}}), .in1(x1q_t), .in2(x2q_t), .in3(x3q_t), .in4(x4q_t), .in5(x5q_t), .in6(x6q_t),
    .in7(x7q_t), .in8(x8q_t), .in9(x9q_t), .in10(x10q_t), .in11(x11q_t), .in12(x12q_t), .in13(x13q_t),
    .in14(x14q_t), .in15(x15q_t), .in16(x16q_t), .in17(x17q_t), .in18(x18q_t), .in19(x19q_t), .in20(x20q_t),
    .in21(x21q_t), .in22(x22q_t), .in23(x23q_t), .in24(x24q_t), .in25(x25q_t), .in26(x26q_t), .in27(x27q_t),
    .in28(x28q_t), .in29(x29q_t), .in30(x30q_t), .in31(x31q_t), .out(rs1), .sel(rsi1));
  Multiplexer #(.select(5), .width(32)) multiplexer_2 (
    .in0({32{1'b0}}), .in1(x1q_t), .in2(x2q_t), .in3(x3q_t), .in4(x4q_t), .in5(x5q_t), .in6(x6q_t),
    .in7(x7q_t), .in8(x8q_t), .in9(x9q_t), .in10(x10q_t), .in11(x11q_t), .in12(x12q_t), .in13(x13q_t),
    .in14(x14q_t), .in15(x15q_t), .in16(x16q_t), .in17(x17q_t), .in18(x18q_t), .in19(x19q_t), .in20(x20q_t),
    .in21(x21q_t), .in22(x22q_t), .in23(x23q_t), .in24(x24q_t), .in25(x25q_t), .in26(x26q_t), .in27(x27q_t),
    .in28(x28q_t), .in29(x29q_t), .in30(x30q_t), .in31(x31q_t), .out(rs2), .sel(rsi2));

  // Other names for the same wires on the sheet: clk_t = clk; rd_t[31:0] = rd; rdi_t[4:0] = rdi; reset_t = reset;
  //   rs1_t[31:0] = rs1; rs2_t[31:0] = rs2; rsi1_t[4:0] = rsi1; rsi2_t[4:0] = rsi2; we_t = we
endmodule

module InstructionMemory (
  input  [13:0] addr,
  output [31:0] data
);

  wire [13:0] adder_1_out, adder_2_out, adder_3_out;

  ROM #(.addrWidth(14)) rom_1 (.addr(addr), .data(data[31:24]));
  ROM #(.addrWidth(14)) rom_2 (.addr(adder_1_out), .data(data[23:16]));
  Adder #(.width(14)) adder_1 (.a(addr), .b(14'h1), .out(adder_1_out));  // open: cin, cout
  ROM #(.addrWidth(14)) rom_3 (.addr(adder_2_out), .data(data[15:8]));
  Adder #(.width(14)) adder_2 (.a(addr), .b(14'h2), .out(adder_2_out));  // open: cin, cout
  ROM #(.addrWidth(14)) rom_4 (.addr(adder_3_out), .data(data[7:0]));
  Adder #(.width(14)) adder_3 (.a(addr), .b(14'h3), .out(adder_3_out));  // open: cin, cout

  // Other names for the same wires on the sheet: addr_t[13:0] = addr; data_3_t[7:0] = data[7:0];
  //   data_2_t[7:0] = data[15:8]; data_1_t[7:0] = data[23:16]; data_0_t[7:0] = data[31:24]

  // Notes on the sheet:
  //   contents of rom_1 (hex, n*v repeats v):
  //   3e 80 0 93 7d 0 81 13 c1 81 1 93 83 1 82 13 3e 82 2 93 0 0 3 13 0 3 24 3 0 c0 3 13 0 80 3 93 0 3 a3
  //   83 0 3 4 3 0 4 84 93 0 93 80 23 0 14 84 93 ff f4 4 13 fe 4 1a e3 0 40 3 13 0 3 23 3 1 0 4 93 0 4 84
  //   3 0 83 0 23 0 14 84 93 0 4 84 3 fe 4 1a e3 0 0 0 13 0 0 0 13 0 0 0 13
  //   contents of rom_2 (hex, n*v repeats v):
  //   3e 80 0 93 7d 0 81 13 c1 81 1 93 83 1 82 13 3e 82 2 93 0 0 3 13 0 3 24 3 0 c0 3 13 0 80 3 93 0 3 a3
  //   83 0 3 4 3 0 4 84 93 0 93 80 23 0 14 84 93 ff f4 4 13 fe 4 1a e3 0 40 3 13 0 3 23 3 1 0 4 93 0 4 84
  //   3 0 83 0 23 0 14 84 93 0 4 84 3 fe 4 1a e3 0 0 0 13 0 0 0 13 0 0 0 13
  //   Instruction Memory
  //   contents of rom_3 (hex, n*v repeats v):
  //   3e 80 0 93 7d 0 81 13 c1 81 1 93 83 1 82 13 3e 82 2 93 0 0 3 13 0 3 24 3 0 c0 3 13 0 80 3 93 0 3 a3
  //   83 0 3 4 3 0 4 84 93 0 93 80 23 0 14 84 93 ff f4 4 13 fe 4 1a e3 0 40 3 13 0 3 23 3 1 0 4 93 0 4 84
  //   3 0 83 0 23 0 14 84 93 0 4 84 3 fe 4 1a e3 0 0 0 13 0 0 0 13 0 0 0 13
  //   contents of rom_4 (hex, n*v repeats v):
  //   3e 80 0 93 7d 0 81 13 c1 81 1 93 83 1 82 13 3e 82 2 93 0 0 3 13 0 3 24 3 0 c0 3 13 0 80 3 93 0 3 a3
  //   83 0 3 4 3 0 4 84 93 0 93 80 23 0 14 84 93 ff f4 4 13 fe 4 1a e3 0 40 3 13 0 3 23 3 1 0 4 93 0 4 84
  //   3 0 83 0 23 0 14 84 93 0 4 84 3 fe 4 1a e3 0 0 0 13 0 0 0 13 0 0 0 13
endmodule

module SignExtender (
  input  [24:0] raw_data,
  input  [2:0] imm_src,
  output [31:0] data_out
);

  wire [12:0] bit_extender_3_out, shifter_3_out;
  wire [20:0] bit_extender_1_out, shifter_2_out;
  wire [24:0] b_type_data, i_type_data, j_type_data, s_type_data, u_type_data;
  wire [31:0] bit_extender_2_out, bit_extender_4_out, bit_extender_5_out, bit_extender_6_out,
       bit_extender_7_out, shifter_1_out;

  assign bit_extender_1_out = {{1{1'b0}}, {j_type_data[24], j_type_data[12:5], j_type_data[13], j_type_data[23:14]}};  // Bit_Extender bit_extender_1
  assign bit_extender_2_out = {{12{u_type_data[24]}}, u_type_data[24:5]};  // Bit_Extender bit_extender_2
  Shifter #(.width(32)) shifter_1 (.in(bit_extender_2_out), .\dist (5'b01100), .out(shifter_1_out));
  Demultiplexer #(.select(3), .width(25)) demultiplexer_1 (
    .out0(i_type_data), .out1(s_type_data), .out2(b_type_data), .out3(j_type_data), .out4(u_type_data),
    .in(raw_data), .sel(imm_src));  // open: out5, out6, out7
  assign bit_extender_3_out = {{1{1'b0}}, {b_type_data[24], b_type_data[0], b_type_data[23:18], b_type_data[4:1]}};  // Bit_Extender bit_extender_3
  Shifter #(.width(21)) shifter_2 (.in(bit_extender_1_out), .\dist (5'b00001), .out(shifter_2_out));
  assign bit_extender_4_out = {{20{i_type_data[24]}}, i_type_data[24:13]};  // Bit_Extender bit_extender_4
  assign bit_extender_5_out = {{20{s_type_data[24]}}, {s_type_data[24:18], s_type_data[4:0]}};  // Bit_Extender bit_extender_5
  assign bit_extender_6_out = {{19{shifter_3_out[12]}}, shifter_3_out};  // Bit_Extender bit_extender_6
  Shifter #(.width(13)) shifter_3 (.in(bit_extender_3_out), .\dist (4'b0001), .out(shifter_3_out));
  assign bit_extender_7_out = {{11{shifter_2_out[20]}}, shifter_2_out};  // Bit_Extender bit_extender_7
  Multiplexer #(.select(3), .width(32)) multiplexer_1 (
    .in0(bit_extender_4_out), .in1(bit_extender_5_out), .in2(bit_extender_6_out), .in3(bit_extender_7_out),
    .in4(shifter_1_out), .out(data_out), .sel(imm_src));  // open: in5, in6, in7

  // Other names for the same wires on the sheet: data_out_t[31:0] = data_out; imm_src_t[2:0] = imm_src;
  //   raw_data_t[24:0] = raw_data

  // Notes on the sheet:
  //   Sign Extender
endmodule

module ProgramCounter (
  input  [13:0] inPC,
  input  clk,
  input  reset,
  output [13:0] outPC
);

  Register #(.trigger("falling"), .width(14)) register_1 (.D(inPC), .en(1'b1), .clk(clk), .Q(outPC), .clr(reset));

  // Other names for the same wires on the sheet: clk_t = clk; inPC_t[13:0] = inPC; outPC_t[13:0] = outPC;
  //   reset_t = reset

  // Notes on the sheet:
  //   Program Counter
endmodule

module DataMemory (
  input  [31:0] addr,
  input  [31:0] wd,
  input  clk,
  input  we,
  input  [3:0] mask,
  output [31:0] data_out
);

  wire mem_sel_t, re_0_t, re_1_t, re_2_t, re_3_t, we_0_t, we_1_t, we_2_t, we_3_t;

  not not_1 (mem_sel_t, addr[31]);
  and and_1 (we_0_t, we, mem_sel_t, mask[0]);
  and and_2 (we_1_t, we, mem_sel_t, mask[1]);
  and and_3 (we_2_t, we, mem_sel_t, mask[2]);
  and and_4 (we_3_t, we, mem_sel_t, mask[3]);
  RAM #(.asyncread("true"), .\type ("nonvolatile")) ram_1 (
    .addr(addr[7:0]), .we(we_3_t), .oe(re_3_t), .clk(clk), .din(wd[31:24]), .dout(data_out[31:24]));
  RAM #(.asyncread("true"), .trigger("falling"), .\type ("nonvolatile")) ram_2 (
    .addr(addr[7:0]), .we(we_1_t), .oe(re_1_t), .clk(clk), .din(wd[15:8]), .dout(data_out[15:8]));
  and and_5 (re_0_t, ~we, mem_sel_t, mask[0]);  // AND_Gate
  and and_6 (re_1_t, ~we, mem_sel_t, mask[1]);  // AND_Gate
  and and_7 (re_2_t, ~we, mem_sel_t, mask[2]);  // AND_Gate
  and and_8 (re_3_t, ~we, mem_sel_t, mask[3]);  // AND_Gate
  RAM #(.asyncread("true"), .trigger("falling"), .\type ("nonvolatile")) ram_3 (
    .addr(addr[7:0]), .we(we_2_t), .oe(re_2_t), .clk(clk), .din(wd[23:16]), .dout(data_out[23:16]));
  RAM #(.asyncread("true"), .trigger("falling"), .\type ("nonvolatile")) ram_4 (
    .addr(addr[7:0]), .we(we_0_t), .oe(re_0_t), .clk(clk), .din(wd[7:0]), .dout(data_out[7:0]));

  // Other names for the same wires on the sheet: addr_0[7:0] = addr[7:0]; addr_1[7:0] = addr[15:8];
  //   addr_2[7:0] = addr[23:16]; addr_3[7:0] = addr[31:24]; clk_t = clk; do_0[7:0] = data_out[7:0];
  //   do_1[7:0] = data_out[15:8]; do_2[7:0] = data_out[23:16]; do_3[7:0] = data_out[31:24]; mask_0_t = mask[0];
  //   mask_1_t = mask[1]; mask_2_t = mask[2]; mask_3_t = mask[3]; wd_0[7:0] = wd[7:0]; wd_1[7:0] = wd[15:8];
  //   wd_2[7:0] = wd[23:16]; wd_3[7:0] = wd[31:24]; we_t = we

  // Notes on the sheet:
  //   Data Memory
endmodule

module ControlLogic (
  input  [6:0] op,
  input  [2:0] func3,
  input  [6:0] func7,
  input  alu_zero,
  input  alu_lb,
  output [3:0] alu_control,
  output alu_src,
  output [2:0] imm_src,
  output [1:0] wb_src,
  output mem_write,
  output pc_src,
  output reg_write,
  output [1:0] second_add_src,
  output data_valid
);

  wire add_sub_t, alu_op_0_t, alu_op_1_t, alu_op_2_t, and_19_out, and_20_out, and_21_out, and_22_out,
       and_23_out, and_24_out, and_25_out, and_26_out, and_27_out, and_28_out, and_29_out, and_30_out,
       and_31_out, and_32_out, and_t, beq_t, bge_t, bgeu_t, blt_t, bltu_t, bne_t, is_auipc_t, is_b_t, is_i_t,
       is_j_t, is_jalr_t, is_load_t, is_lui_t, is_r_t, is_u_t, not_2_out, or_2_out, or_3_out, or_4_out,
       or_6_out, or_7_out, or_9_out, or_10_out, or_11_out, or_12_out, or_t, sll_t, slt_t, sltu_t, snd_0_src,
       srl_sra_t, xor_t;
  wire [1:0] alu_op_t;
  wire [3:0] alu_branch_t, alu_math_t;

  and and_1 (is_r_t, op[0], op[1], ~op[2], ~op[3], op[4], op[5], ~op[6]);  // AND_Gate
  and and_2 (is_i_t, op[0], op[1], ~op[2], ~op[3], op[4], ~op[5], ~op[6]);  // AND_Gate
  and and_3 (is_load_t, op[0], op[1], ~op[2], ~op[3], ~op[4], ~op[5], ~op[6]);  // AND_Gate
  and and_4 (is_jalr_t, op[0], op[1], op[2], ~op[3], ~op[4], op[5], op[6]);  // AND_Gate
  or or_1 (is_u_t, is_lui_t, is_auipc_t);
  and and_5 (mem_write, op[0], op[1], ~op[2], ~op[3], ~op[4], op[5], ~op[6]);  // AND_Gate
  and and_6 (is_b_t, op[0], op[1], ~op[2], ~op[3], ~op[4], op[5], op[6]);  // AND_Gate
  and and_7 (is_lui_t, op[0], op[1], op[2], ~op[3], op[4], op[5], ~op[6]);  // AND_Gate
  and and_8 (is_auipc_t, op[0], op[1], op[2], ~op[3], op[4], ~op[5], ~op[6]);  // AND_Gate
  and and_9 (is_j_t, op[0], op[1], op[2], op[3], ~op[4], op[5], op[6]);  // AND_Gate
  and and_10 (reg_write, ~mem_write, ~is_b_t);  // AND_Gate
  nor nor_1 (alu_src, is_r_t, is_b_t);
  not not_1 (data_valid, is_load_t);
  Decoder #(.select(2)) decoder_1 (
    .out0(alu_op_0_t), .out1(alu_op_1_t), .out2(alu_op_2_t), .sel(alu_op_t));  // open: out3, en
  and and_11 (add_sub_t, ~func3[0], ~func3[1], ~func3[2]);  // AND_Gate
  and and_12 (sll_t, func3[0], ~func3[1], ~func3[2]);  // AND_Gate
  and and_13 (slt_t, ~func3[0], func3[1], ~func3[2]);  // AND_Gate
  and and_14 (sltu_t, func3[0], func3[1], ~func3[2]);  // AND_Gate
  and and_15 (xor_t, ~func3[0], ~func3[1], func3[2]);  // AND_Gate
  and and_16 (srl_sra_t, func3[0], ~func3[1], func3[2]);  // AND_Gate
  and and_17 (or_t, ~func3[0], func3[1], func3[2]);  // AND_Gate
  and and_18 (and_t, func3[0], func3[1], func3[2]);
  or or_2 (or_2_out, is_load_t, is_i_t);
  Priority_Encoder priority_encoder_1 (
    .in0(or_2_out), .in1(mem_write), .in2(is_b_t), .in3(is_j_t), .in4(is_u_t), .out(imm_src));  // open: in5, in6, in7, en_in, gs, en_out
  or or_3 (or_3_out, is_load_t, mem_write);
  or or_4 (or_4_out, is_r_t, is_i_t);
  Priority_Encoder #(.select(2)) priority_encoder_2 (
    .in0(or_3_out), .in1(is_b_t), .in2(or_4_out), .out(alu_op_t));  // open: in3, gs, en_out, en_in
  assign alu_control = alu_op_0_t ? 4'b0000 : 4'bz;  // Controlled_Buffer controlled_buffer_1
  assign alu_control = alu_op_1_t ? alu_branch_t : 4'bz;  // Controlled_Buffer controlled_buffer_2
  assign alu_control = alu_op_2_t ? alu_math_t : 4'bz;  // Controlled_Buffer controlled_buffer_3
  assign alu_math_t = and_19_out ? 4'b0000 : 4'bz;  // Controlled_Buffer controlled_buffer_4
  and and_19 (and_19_out, add_sub_t, ~op[5]);  // AND_Gate
  assign alu_math_t = and_20_out ? 4'b0000 : 4'bz;  // Controlled_Buffer controlled_buffer_5
  and and_20 (and_20_out, add_sub_t, and_21_out);
  and and_21 (and_21_out, func7[5], ~op[5]);  // AND_Gate
  assign alu_math_t = and_22_out ? 4'b0001 : 4'bz;  // Controlled_Buffer controlled_buffer_6
  and and_22 (and_22_out, add_sub_t, and_23_out);
  and and_23 (and_23_out, func7[5], op[5]);
  assign alu_math_t = and_t ? 4'b0010 : 4'bz;  // Controlled_Buffer controlled_buffer_7
  assign alu_math_t = or_t ? 4'b0011 : 4'bz;  // Controlled_Buffer controlled_buffer_8
  assign alu_math_t = sll_t ? 4'b0100 : 4'bz;  // Controlled_Buffer controlled_buffer_9
  assign alu_math_t = slt_t ? 4'b0101 : 4'bz;  // Controlled_Buffer controlled_buffer_10
  assign alu_math_t = and_24_out ? 4'b0110 : 4'bz;  // Controlled_Buffer controlled_buffer_11
  and and_24 (and_24_out, srl_sra_t, ~func7[5]);  // AND_Gate
  assign alu_math_t = sltu_t ? 4'b0111 : 4'bz;  // Controlled_Buffer controlled_buffer_12
  assign alu_math_t = xor_t ? 4'b1000 : 4'bz;  // Controlled_Buffer controlled_buffer_13
  assign alu_math_t = and_25_out ? 4'b1001 : 4'bz;  // Controlled_Buffer controlled_buffer_14
  and and_25 (and_25_out, srl_sra_t, func7[5]);
  and and_26 (and_26_out, beq_t, alu_zero);
  and and_27 (and_27_out, bne_t, ~alu_zero);  // AND_Gate
  and and_28 (and_28_out, blt_t, alu_lb);
  and and_29 (and_29_out, bge_t, ~alu_lb);  // AND_Gate
  and and_30 (and_30_out, bltu_t, alu_lb);
  and and_31 (and_31_out, bltu_t, ~alu_lb);  // AND_Gate
  Priority_Encoder #(.select(2)) priority_encoder_3 (
    .in0(snd_0_src), .in1(is_lui_t), .in2(is_jalr_t), .out(second_add_src));  // open: in3, gs, en_out, en_in
  or or_5 (snd_0_src, is_b_t, is_j_t, is_auipc_t);
  or or_6 (or_6_out, and_26_out, and_27_out, and_28_out, and_29_out, and_30_out, and_31_out);
  or or_7 (or_7_out, is_j_t, is_jalr_t);
  and and_32 (and_32_out, or_6_out, is_b_t);
  or or_8 (pc_src, and_32_out, or_7_out);
  and and_33 (beq_t, ~func3[0], ~func3[1], ~func3[2]);  // AND_Gate
  and and_34 (bne_t, func3[0], ~func3[1], ~func3[2]);  // AND_Gate
  and and_35 (blt_t, ~func3[0], func3[1], ~func3[2]);  // AND_Gate
  and and_36 (bge_t, func3[0], func3[1], ~func3[2]);  // AND_Gate
  and and_37 (bltu_t, ~func3[0], ~func3[1], func3[2]);  // AND_Gate
  and and_38 (bgeu_t, func3[0], ~func3[1], func3[2]);  // AND_Gate
  assign alu_branch_t = or_9_out ? 4'b0001 : 4'bz;  // Controlled_Buffer controlled_buffer_15
  or or_9 (or_9_out, beq_t, bne_t);
  assign alu_branch_t = or_10_out ? 4'b0101 : 4'bz;  // Controlled_Buffer controlled_buffer_16
  or or_10 (or_10_out, blt_t, bge_t);
  assign alu_branch_t = or_11_out ? 4'b0111 : 4'bz;  // Controlled_Buffer controlled_buffer_17
  or or_11 (or_11_out, bltu_t, bgeu_t);
  or or_12 (or_12_out, is_j_t, is_jalr_t);
  not not_2 (not_2_out, is_load_t);
  Priority_Encoder #(.select(2)) priority_encoder_4 (
    .in0(not_2_out), .in1(is_load_t), .in2(or_12_out), .in3(is_u_t), .out(wb_src));  // open: gs, en_out, en_in

  // Other names for the same wires on the sheet: alu_0_t = alu_zero; alu_ctrl_t[3:0] = alu_control; alu_lb_t = alu_lb;
  //   alu_src_t = alu_src; func_7_5_t = func7[5]; func_3_0_t = func3[0]; func_3_t[2:0] = func3; func_3_1_t = func3[1];
  //   func_3_2_t = func3[2]; imm_src_t[2:0] = imm_src; is_s_t = mem_write; jmp_t = is_j_t; op_0_t = op[0];
  //   op_t[6:0] = op; op_1_t = op[1]; op_2_t = op[2]; op_3_t = op[3]; op_4_t = op[4]; op_5_t = op[5]; op_6_t = op[6];
  //   pc_src_t = pc_src; reg_w_t = reg_write; scnd_add_src_t[1:0] = second_add_src; w_back_src_t[1:0] = wb_src

  // Notes on the sheet:
  //   R-type
  //   I-type
  //   load-type
  //   jalr-type
  //   U-type
  //   Jumping
  //   Instruction Type Detection
  //   S-type
  //   B-type
  //   lui-type
  //   auipc-type
  //   J-type
  //   Immediate Source
  //   ALU Decoder
  //   Math Operations
  //   ALU Operation
  //   Branching
  //   Second Add Source
  //   Branch Operations
  //   Write Back
endmodule

module LoadStoreDecoder (
  input  [31:0] alu_addr,
  input  [2:0] f3,
  input  [31:0] reg_read,
  output [3:0] byte_enable,
  output [31:0] data
);

  wire b_t, correct_w_t, frth_b_t, fst_b_t, fst_h_t, h_t, snd_b_t, snd_h_t, trd_b_t, w_t;
  wire [1:0] offset_t;
  wire [3:0] b_mask_t, h_mask_t, w_mask_t;
  wire [31:0] and_1_out, and_3_out, b_data_t, h_data_t, shifter_2_out, shifter_3_out, shifter_4_out,
       shifter_6_out, w_data_t;
  wire [31:2] and_2_out;

  Decoder #(.select(2)) decoder_1 (.out0(b_t), .out1(h_t), .out2(w_t), .sel(f3[1:0]));  // open: out3, en
  Shifter #(.width(4)) shifter_1 (.in(4'b0001), .\dist (offset_t), .out(b_mask_t));
  Decoder #(.select(2)) decoder_2 (
    .out0(fst_b_t), .out1(snd_b_t), .out2(trd_b_t), .out3(frth_b_t), .sel(offset_t));  // open: en
  assign and_1_out = reg_read & 32'hff;  // AND_Gate and_1, 32 bits wide
  assign b_data_t = fst_b_t ? and_1_out : 32'bz;  // Controlled_Buffer controlled_buffer_1
  Shifter #(.width(32)) shifter_2 (.in(and_1_out), .\dist (5'b01000), .out(shifter_2_out));
  Shifter #(.width(32)) shifter_3 (.in(and_1_out), .\dist (5'b10000), .out(shifter_3_out));
  Shifter #(.width(32)) shifter_4 (.in(and_1_out), .\dist (5'b11000), .out(shifter_4_out));
  assign b_data_t = snd_b_t ? shifter_2_out : 32'bz;  // Controlled_Buffer controlled_buffer_2
  assign b_data_t = trd_b_t ? shifter_3_out : 32'bz;  // Controlled_Buffer controlled_buffer_3
  assign b_data_t = frth_b_t ? shifter_4_out : 32'bz;  // Controlled_Buffer controlled_buffer_4
  assign {and_2_out, offset_t} = alu_addr & 32'h3;  // AND_Gate and_2, 32 bits wide
  assign data = b_t ? b_data_t : 32'bz;  // Controlled_Buffer controlled_buffer_5
  assign data = h_t ? h_data_t : 32'bz;  // Controlled_Buffer controlled_buffer_6
  assign data = w_t ? w_data_t : 32'bz;  // Controlled_Buffer controlled_buffer_7
  assign and_3_out = reg_read & 32'hffff;  // AND_Gate and_3, 32 bits wide
  Shifter #(.width(4)) shifter_5 (.in(4'b0011), .\dist (offset_t), .out(h_mask_t));
  assign h_data_t = fst_h_t ? and_3_out : 32'bz;  // Controlled_Buffer controlled_buffer_8
  Decoder #(.select(2)) decoder_3 (.out0(fst_h_t), .out2(snd_h_t), .sel(offset_t));  // open: out1, out3, en
  assign byte_enable = b_t ? b_mask_t : 4'bz;  // Controlled_Buffer controlled_buffer_9
  assign byte_enable = h_t ? h_mask_t : 4'bz;  // Controlled_Buffer controlled_buffer_10
  assign byte_enable = w_t ? w_mask_t : 4'bz;  // Controlled_Buffer controlled_buffer_11
  assign h_data_t = snd_h_t ? shifter_6_out : 32'bz;  // Controlled_Buffer controlled_buffer_12
  Shifter #(.width(32)) shifter_6 (.in(and_3_out), .\dist (5'b10000), .out(shifter_6_out));
  Decoder #(.select(2)) decoder_4 (.out0(correct_w_t), .sel(offset_t));  // open: out1, out2, out3, en
  assign w_mask_t = correct_w_t ? 4'b1111 : 4'bz;  // Controlled_Buffer controlled_buffer_13
  assign w_data_t = correct_w_t ? reg_read : 32'bz;  // Controlled_Buffer controlled_buffer_14

  // Other names for the same wires on the sheet: addr_t[31:0] = alu_addr; data_t[31:0] = data; f3_t[2:0] = f3;
  //   mask_t[3:0] = byte_enable; reg_data_t[31:0] = reg_read

  // Notes on the sheet:
  //   Data Type
  //   Byte
  //   Load Store Decoder
  //   Half
  //   Word
endmodule

module Reader (
  input  [31:0] mem_data,
  input  [3:0] mask,
  input  [2:0] f3,
  output [31:0] wb_data,
  output valid
);

  wire and_1_out, and_2_out, and_3_out, and_4_out, and_5_out, and_6_out, b_t, h_t, or_1_out, or_2_out, sign,
       w_t;
  wire [31:0] b_data_t, bit_extender_1_out, bit_extender_2_out, controlled_buffer_1_out,
       controlled_buffer_6_out, controlled_buffer_8_out, controlled_buffer_9_out, controlled_buffer_16_out,
       controlled_buffer_17_out, h_data_t, masked_data_t, shifter_1_out, shifter_2_out, shifter_3_out,
       shifter_4_out, w_data_t;

  Decoder #(.select(2)) decoder_1 (.out0(b_t), .out1(h_t), .out2(w_t), .sel(f3[1:0]));  // open: out3, en
  not not_1 (sign, f3[2]);
  assign controlled_buffer_1_out = h_t ? masked_data_t : 32'bz;  // Controlled_Buffer controlled_buffer_1
  assign masked_data_t[7:0] = mask[0] ? mem_data[7:0] : 8'bz;  // Controlled_Buffer controlled_buffer_2
  assign masked_data_t[15:8] = mask[1] ? mem_data[15:8] : 8'bz;  // Controlled_Buffer controlled_buffer_3
  assign masked_data_t[23:16] = mask[2] ? mem_data[23:16] : 8'bz;  // Controlled_Buffer controlled_buffer_4
  assign masked_data_t[31:24] = mask[3] ? mem_data[31:24] : 8'bz;  // Controlled_Buffer controlled_buffer_5
  assign controlled_buffer_6_out = b_t ? masked_data_t : 32'bz;  // Controlled_Buffer controlled_buffer_6
  Shifter #(.shift("lr"), .width(32)) shifter_1 (.in(controlled_buffer_1_out), .\dist (5'b10000), .out(shifter_1_out));
  assign w_data_t = w_t ? masked_data_t : 32'bz;  // Controlled_Buffer controlled_buffer_7
  Shifter #(.shift("lr"), .width(32)) shifter_2 (.in(controlled_buffer_6_out), .\dist (5'b01000), .out(shifter_2_out));
  Shifter #(.shift("lr"), .width(32)) shifter_3 (.in(controlled_buffer_6_out), .\dist (5'b10000), .out(shifter_3_out));
  Shifter #(.shift("lr"), .width(32)) shifter_4 (.in(controlled_buffer_6_out), .\dist (5'b11000), .out(shifter_4_out));
  assign controlled_buffer_8_out = mask[0] ? controlled_buffer_1_out : 32'bz;  // Controlled_Buffer controlled_buffer_8
  assign controlled_buffer_9_out = mask[2] ? shifter_1_out : 32'bz;  // Controlled_Buffer controlled_buffer_9
  assign b_data_t = mask[0] ? controlled_buffer_6_out : 32'bz;  // Controlled_Buffer controlled_buffer_10
  assign b_data_t = mask[1] ? shifter_2_out : 32'bz;  // Controlled_Buffer controlled_buffer_11
  assign b_data_t = mask[2] ? shifter_3_out : 32'bz;  // Controlled_Buffer controlled_buffer_12
  assign b_data_t = mask[3] ? shifter_4_out : 32'bz;  // Controlled_Buffer controlled_buffer_13
  assign h_data_t = mask[1] ? controlled_buffer_8_out : 32'bz;  // Controlled_Buffer controlled_buffer_14
  assign h_data_t = mask[3] ? controlled_buffer_9_out : 32'bz;  // Controlled_Buffer controlled_buffer_15
  and and_1 (and_1_out, mask[0], mask[1]);
  and and_2 (and_2_out, mask[2], mask[3]);
  assign controlled_buffer_16_out = b_t ? b_data_t : 32'bz;  // Controlled_Buffer controlled_buffer_16
  assign controlled_buffer_17_out = h_t ? h_data_t : 32'bz;  // Controlled_Buffer controlled_buffer_17
  assign wb_data = w_t ? w_data_t : 32'bz;  // Controlled_Buffer controlled_buffer_18
  or or_1 (or_1_out, mask[0], mask[1], mask[2], mask[3]);
  and and_3 (and_3_out, or_1_out, b_t);
  or or_2 (or_2_out, and_1_out, and_2_out);
  and and_4 (and_4_out, or_2_out, h_t);
  and and_5 (and_5_out, mask[0], mask[1], mask[2], mask[3]);
  and and_6 (and_6_out, and_5_out, w_t);
  assign bit_extender_1_out = {{24{controlled_buffer_16_out[7]}}, controlled_buffer_16_out[7:0]};  // Bit_Extender bit_extender_1
  assign bit_extender_2_out = {{16{controlled_buffer_17_out[15]}}, controlled_buffer_17_out[15:0]};  // Bit_Extender bit_extender_2
  assign wb_data = sign ? bit_extender_1_out : 32'bz;  // Controlled_Buffer controlled_buffer_19
  assign wb_data = f3[2] ? controlled_buffer_16_out : 32'bz;  // Controlled_Buffer controlled_buffer_20
  assign wb_data = sign ? bit_extender_2_out : 32'bz;  // Controlled_Buffer controlled_buffer_21
  assign wb_data = f3[2] ? controlled_buffer_17_out : 32'bz;  // Controlled_Buffer controlled_buffer_22
  or or_3 (valid, and_3_out, and_4_out, and_6_out);

  // Other names for the same wires on the sheet: data_t[31:0] = mem_data; f3_t[2:0] = f3; unsign = f3[2];
  //   final_data_t[31:0] = wb_data; mask_0_t = mask[0]; mask_t[3:0] = mask; mask_1_t = mask[1]; mask_2_t = mask[2];
  //   mask_3_t = mask[3]

  // Notes on the sheet:
  //   Data Type
  //   Reader
  //   Byte
  //   Half
  //   Word
endmodule
