// Logisim project project.circ as structural Verilog: 4 circuits, main circuit main
module main (
  input  in_1
);

  wire clk_1_clock_out, clock_1_out;
  wire [7:0] pc_1_always_out, pull_resistor_6_node;

  Clock clock_1 (.out(clock_1_out));
  CLK clk_1 (.CLOCK_IN(clock_1_out), .CLOCK_ENABLE(in_1), .CLOCK_OUT(clk_1_clock_out));  // open: MANUAL_TICK, HALT
  LED led_1 ();  // open: in
  LED led_2 ();  // open: in
  Pull_Resistor pull_resistor_1 (.node(pull_resistor_6_node[7]));
  LED led_3 ();  // open: in
  LED led_4 ();  // open: in
  LED led_5 ();  // open: in
  LED led_6 ();  // open: in
  Pull_Resistor pull_resistor_2 (.node(pull_resistor_6_node[6]));
  Pull_Resistor pull_resistor_3 (.node(pull_resistor_6_node[5]));
  Pull_Resistor pull_resistor_4 (.node(pull_resistor_6_node[4]));
  Pull_Resistor pull_resistor_5 (.node(pull_resistor_6_node[3]));
  LED led_7 ();  // open: in
  LED led_8 ();  // open: in
  Pull_Resistor pull_resistor_6 (.node(pull_resistor_6_node[0]));
  Pull_Resistor pull_resistor_7 (.node(pull_resistor_6_node[2]));
  Pull_Resistor pull_resistor_8 (.node(pull_resistor_6_node[1]));
  LED led_9 ();  // open: in
  LED led_10 ();  // open: in
  LED led_11 ();  // open: in
  LED led_12 ();  // open: in
  PC pc_1 (
    .CLOCK(clk_1_clock_out), .ADDRESS_IN(pull_resistor_6_node), .ADDRESS_OUT(pull_resistor_6_node),
    .ALWAYS_OUT(pc_1_always_out));  // open: RESET, JUMP, COUNTER_OUT, COUNTER_ENABLE
  LED led_13 ();  // open: in
  LED led_14 ();  // open: in
  LED led_15 ();  // open: in
  LED led_16 ();  // open: in
  ACCUMULATOR accumulator_1 (
    .CLOCK(clk_1_clock_out), .DATA_IN(pull_resistor_6_node), .DATA_OUT(pull_resistor_6_node));  // open: A_WRITE, A_READ, RESET, ALWAYS_OUT

  // Notes on the sheet:
  //   BUS
endmodule

module CLK (
  input  CLOCK_IN,
  input  CLOCK_ENABLE,
  input  MANUAL_TICK,
  input  HALT,
  output CLOCK_OUT
);

  wire and_1_out, and_2_out, not_1_out, not_2_out, or_1_out;

  not not_1 (not_1_out, CLOCK_ENABLE);
  and and_1 (and_1_out, CLOCK_IN, CLOCK_ENABLE);
  and and_2 (and_2_out, not_1_out, MANUAL_TICK);
  or or_1 (or_1_out, and_1_out, and_2_out);
  not not_2 (not_2_out, HALT);
  and and_3 (CLOCK_OUT, or_1_out, not_2_out);
endmodule

module PC (
  input  RESET,
  input  JUMP,
  input  COUNTER_ENABLE,
  input  CLOCK,
  input  [7:0] ADDRESS_IN,
  input  COUNTER_OUT,
  output [7:0] ALWAYS_OUT,
  output [7:0] ADDRESS_OUT
);

  Counter counter_1 (
    .clr(RESET), .load(JUMP), .up(COUNTER_ENABLE), .count(COUNTER_ENABLE), .clk(CLOCK), .D(ADDRESS_IN),
    .Q(ALWAYS_OUT));  // open: carry
  assign ADDRESS_OUT = COUNTER_OUT ? ALWAYS_OUT : 8'bz;  // Controlled_Buffer controlled_buffer_1
endmodule

module ACCUMULATOR (
  input  [7:0] DATA_IN,
  input  A_WRITE,
  input  A_READ,
  input  CLOCK,
  input  RESET,
  output [7:0] ALWAYS_OUT,
  output [7:0] DATA_OUT
);

  Register register_1 (.D(DATA_IN), .en(A_WRITE), .clk(CLOCK), .Q(ALWAYS_OUT), .clr(RESET));
  assign DATA_OUT = A_READ ? ALWAYS_OUT : 8'bz;  // Controlled_Buffer controlled_buffer_1
endmodule
